// Logisim project multiplexer.circ as structural Verilog: 2 circuits, main circuit 2_to_1
module _2_to_1 (
  input  A,
  input  S,
  input  B,
  output out_4
);

  wire and_1_out, and_2_out, not_1_out;

  not not_1 (not_1_out, S);
  and and_1 (and_1_out, A, not_1_out);
  and and_2 (and_2_out, S, B);
  or or_1 (out_4, and_1_out, and_2_out);
endmodule

module _4_to_1 (
  input  in_00,
  input  in_01,
  input  in_10,
  input  in_11,
  input  sel_0,
  input  sel_1,
  output out
);

  wire n2_to_1_1_out_4, n2_to_1_2_out_4;

  _2_to_1 u_2_to_1_1 (.A(in_00), .S(sel_1), .B(in_01), .out_4(n2_to_1_1_out_4));
  _2_to_1 u_2_to_1_2 (.A(in_10), .S(sel_1), .B(in_11), .out_4(n2_to_1_2_out_4));
  _2_to_1 u_2_to_1_3 (.A(n2_to_1_1_out_4), .S(sel_0), .B(n2_to_1_2_out_4), .out_4(out));
endmodule
