// Logisim project xor.circ as structural Verilog: 2 circuits, main circuit 2-to-1
module _2_to_1 (
  input  A,
  input  B,
  output S
);

  wire and_1_out, and_2_out, not_1_out, not_2_out;

  not not_1 (not_1_out, A);
  not not_2 (not_2_out, B);
  and and_1 (and_1_out, not_1_out, B);
  and and_2 (and_2_out, A, not_2_out);
  or or_1 (S, and_1_out, and_2_out);
endmodule

module _4_to_1 (
  input  in_00,
  input  in_01,
  input  in_10,
  input  in_11,
  output out
);

  wire n2_to_1_1_s, n2_to_1_2_s;

  _2_to_1 u_2_to_1_1 (.A(in_00), .B(in_01), .S(n2_to_1_1_s));
  _2_to_1 u_2_to_1_2 (.A(in_10), .B(in_11), .S(n2_to_1_2_s));
  _2_to_1 u_2_to_1_3 (.A(n2_to_1_1_s), .B(n2_to_1_2_s), .S(out));
endmodule
